# Fritzing sketch 4dig_7seg_led_display_arduino (saved by Fritzing 0.9.2b)
breadboards: 1

parts:
  LED1 = 7-SEGMENT-4DIGIT-YOUNGSUN [package=7-segment-4digit-youngsun-longpads]
  Onderdeel1 = Arduino Uno (Rev3)

nets:
  N1: LED1.DIG1, Onderdeel1.D10_PWM/SS
  N2: LED1.DIG2, Onderdeel1.D11_PWM/MOSI
  N3: LED1.D, Onderdeel1.D5_PWM
  N4: LED1.E, Onderdeel1.D6_PWM
  N5: LED1.DIG3, Onderdeel1.D12/MISO
  N6: LED1.DP, Onderdeel1.D9_PWM
  N7: LED1.DIG4, Onderdeel1.D13/SCK
  N8: LED1.F, Onderdeel1.D7
  N9: LED1.C, Onderdeel1.D4
  N10: LED1.A, Onderdeel1.D2
  N11: LED1.G, Onderdeel1.D8
  N12: LED1.B, Onderdeel1.D3_PWM
