# Fritzing sketch 8led_shiftout_arduino (saved by Fritzing 0.9.2b)
breadboards: 2

parts:
  Onderdeel1 = Arduino Uno (Rev3)
  U1 = 74HC595 [package="DIP16 [THT]"]
  LED1 = LED - 5mm [color="Red (633nm)" package="5 mm [THT]"]
  LED2 = LED - 5mm [color="Red (633nm)" package="5 mm [THT]"]
  LED3 = LED - 5mm [color="Red (633nm)" package="5 mm [THT]"]
  LED4 = LED - 5mm [color="Red (633nm)" package="5 mm [THT]"]
  LED5 = LED - 5mm [color="Red (633nm)" package="5 mm [THT]"]
  LED6 = LED - 5mm [color="Red (633nm)" package="5 mm [THT]"]
  LED7 = LED - 5mm [color="Red (633nm)" package="5 mm [THT]"]
  LED8 = LED - 5mm [color="Red (633nm)" package="5 mm [THT]"]
  R1 = Resistor [tolerance=±5% resistance=220 package=THT]

nets:
  GND: Onderdeel1.GND, U1.GND, R1.Pin_1
  VIN: Onderdeel1.VIN, U1.VCC
  N1: U1.Q1, LED7.anode
  N2: U1.Q2, LED6.anode
  N3: U1.Q3, LED5.anode
  N4: U1.Q4, LED4.anode
  N5: U1.Q5, LED3.anode
  N6: U1.Q6, LED2.anode
  N7: U1.Q7, LED1.anode
  N8: U1.Q0, LED8.anode
  N9: LED8.cathode, R1.Pin_0
