# Fritzing sketch leds_piezo_arduino (saved by Fritzing 0.9.2b)
breadboards: 1

parts:
  Onderdeel1 = Arduino Uno (Rev3)
  LED1 = LED - 5mm [color="Red (633nm)" package="5 mm [THT]"]
  LED2 = LED - 5mm [color="Red (633nm)" package="5 mm [THT]"]
  J1 = Piezo Speaker
  R1 = Resistor [tolerance=±5% resistance=220 package=THT]
  R2 = Resistor [tolerance=±5% resistance=220 package=THT]
  R3 = Resistor [tolerance=±5% resistance=100 package=THT]

nets:
  N1: Onderdeel1.D2, LED1.anode
  N2: Onderdeel1.D3_PWM, J1.pin2
  N3: Onderdeel1.D4, LED2.anode
  N4: Onderdeel1.GND, R1.Pin_1, R2.Pin_1, R3.Pin_1
  N5: LED1.cathode, R2.Pin_0
  N6: LED2.cathode, R1.Pin_0
  N7: J1.pin1, R3.Pin_0
