# Fritzing sketch ontwerp_1 (saved by Fritzing 0.9.3b)
breadboards: 1

parts:
  Part1 = Arduino Uno (Rev3)
  LED1 = LED - 5mm [color="Red (633nm)" package="5 mm [THT]"]
  R1 = Resistor [tolerance=±5% resistance=220 package=THT]
  R2 = Resistor [tolerance=±5% resistance=220 package=THT]
  LED2 = LED - 5mm [color="Red (633nm)" package="5 mm [THT]"]
  J1 = Piezo Speaker

nets:
  N1: Part1.D2, LED1.anode
  N2: Part1.D3_PWM, LED2.anode
  N3: Part1.D4, J1.pin1
  N4: Part1.GND, R1.Pin_0, R2.Pin_0, J1.pin2
  N5: LED1.cathode, R1.Pin_1
  N6: R2.Pin_1, LED2.cathode
