# Fritzing sketch ontwerp_5 (saved by Fritzing 0.9.3b)
breadboards: 1

parts:
  U1 = 74HC595 [package="DIP16 [THT]"]
  U2 = 74HC595 [package="DIP16 [THT]"]
  Part2 = Arduino Uno (Rev3)

nets:
  GND: U1.GND, U1.OE, U2.GND, U2.OE, Part2.GND
  N1: U1.Q7', U2.DS
  VCC: U1.MR, U1.VCC, U2.MR, U2.VCC, Part2.5V
  N2: U1.SH_CP, U2.SH_CP, Part2.D2
  N3: U1.ST_CP, U2.ST_CP, Part2.3V3
  N4: U1.DS, Part2.D3_PWM
