# Fritzing sketch ontwerp_eind (saved by Fritzing 0.9.2b)
breadboards: 3

parts:
  U1 = 74HC595 [package="DIP16 [THT]"]
  U2 = 74HC595 [package="DIP16 [THT]"]
  U3 = 74HC595 [package="DIP16 [THT]"]
  LED1 = LED - 5mm [color="Red (633nm)" package="5 mm [THT]"]
  LED2 = LED - 5mm [color="Red (633nm)" package="5 mm [THT]"]
  LED3 = LED - 5mm [color="Red (633nm)" package="5 mm [THT]"]
  LED4 = LED - 5mm [color="Red (633nm)" package="5 mm [THT]"]
  LED5 = LED - 5mm [color="Red (633nm)" package="5 mm [THT]"]
  LED6 = LED - 5mm [color="Red (633nm)" package="5 mm [THT]"]
  LED7 = LED - 5mm [color="Red (633nm)" package="5 mm [THT]"]
  LED8 = LED - 5mm [color="Red (633nm)" package="5 mm [THT]"]
  R1 = Resistor [tolerance=±5% resistance=220 package=THT]
  R2 = Resistor [tolerance=±5% resistance=220 package=THT]
  R3 = Resistor [tolerance=±5% resistance=220 package=THT]
  R4 = Resistor [tolerance=±5% resistance=220 package=THT]
  R5 = Resistor [tolerance=±5% resistance=220 package=THT]
  R6 = Resistor [tolerance=±5% resistance=220 package=THT]
  R7 = Resistor [tolerance=±5% resistance=220 package=THT]
  R8 = Resistor [tolerance=±5% resistance=220 package=THT]
  S1 = Pushbutton [package="[THT]"]
  S2 = Pushbutton [package="[THT]"]
  S3 = Pushbutton [package="[THT]"]
  S4 = Pushbutton [package="[THT]"]
  S5 = Pushbutton [package="[THT]"]
  S6 = Pushbutton [package="[THT]"]
  S7 = Pushbutton [package="[THT]"]
  S8 = Pushbutton [package="[THT]"]
  J1 = Piezo Speaker
  R9 = Resistor [tolerance=±5% resistance=100 package=THT]
  R10 = Resistor [tolerance=±5% resistance=220 package=THT]
  R11 = Resistor [tolerance=±5% resistance=220 package=THT]
  R12 = Resistor [tolerance=±5% resistance=220 package=THT]
  R13 = Resistor [tolerance=±5% resistance=220 package=THT]
  R14 = Resistor [tolerance=±5% resistance=220 package=THT]
  R15 = Resistor [tolerance=±5% resistance=220 package=THT]
  R16 = Resistor [tolerance=±5% resistance=220 package=THT]
  R17 = Resistor [tolerance=±5% resistance=220 package=THT]
  LED9 = 7-SEGMENT-4DIGIT-YOUNGSUN [package=7-segment-4digit-youngsun]
  LED10 = 7-SEGMENT-4DIGIT-YOUNGSUN [package=7-segment-4digit-youngsun]
  Onderdeel1 = Arduino Uno (Rev3)

nets:
  N1: U1.Q1, LED9.B
  N2: U1.Q2, LED9.C
  N3: U1.Q3, LED9.D
  N4: U1.Q4, LED9.E
  N5: U1.Q5, LED9.F
  N6: U1.Q6, LED9.G
  N7: U1.Q7, LED9.DP
  GND: U1.GND, U3.GND
  N8: U1.Q7', U2.DS
  N9: U1.SH_CP, U3.SH_CP, Onderdeel1.D13/SCK
  N10: U1.ST_CP, U3.ST_CP, Onderdeel1.D8
  N11: U1.DS, Onderdeel1.D12/MISO
  N12: U1.Q0, LED9.A
  VCC: U1.VCC, U2.VCC, U3.VCC, S1.Pin_3, S1.Pin_4, S2.Pin_3, S2.Pin_4, S3.Pin_3, S3.Pin_4, S4.Pin_3, S4.Pin_4, S5.Pin_3, S5.Pin_4, S6.Pin_3, S6.Pin_4, S7.Pin_3, S7.Pin_4, S8.Pin_3, S8.Pin_4, Onderdeel1.A2, Onderdeel1.A3, Onderdeel1.A4/SDA, Onderdeel1.A5/SCL, Onderdeel1.5V
  N13: U2.Q1, LED10.B
  N14: U2.Q2, LED10.C
  N15: U2.Q3, LED10.D
  N16: U2.Q4, LED10.E
  N17: U2.Q5, LED10.F
  N18: U2.Q6, LED10.G
  N19: U2.Q7, LED10.DP
  GND_2: U2.GND, R1.Pin_0, R2.Pin_0, R3.Pin_0, R4.Pin_0, R5.Pin_0, R6.Pin_0, R7.Pin_0, R8.Pin_0, R9.Pin_1, R10.Pin_0, R11.Pin_0, R12.Pin_0, R13.Pin_0, R14.Pin_0, R15.Pin_0, R16.Pin_0, R17.Pin_0, Onderdeel1.GND
  N20: U2.Q7', U3.DS
  N21: U2.Q0, LED10.A
  N22: U3.Q1, LED9.DIG2
  N23: U3.Q2, LED9.DIG3
  N24: U3.Q3, LED9.DIG4
  N25: U3.Q4, LED10.DIG1
  N26: U3.Q5, LED10.DIG2
  N27: U3.Q6, LED10.DIG3
  N28: U3.Q7, LED10.DIG4
  N29: U3.Q0, LED9.DIG1
  N30: LED1.cathode, R8.Pin_1
  N31: LED1.anode, Onderdeel1.D0/RX
  N32: LED2.cathode, R7.Pin_1
  N33: LED2.anode, Onderdeel1.D1/TX
  N34: LED3.cathode, R6.Pin_1
  N35: LED3.anode, Onderdeel1.D2
  N36: LED4.cathode, R5.Pin_1
  N37: LED4.anode, Onderdeel1.D3_PWM
  N38: LED5.cathode, R4.Pin_1
  N39: LED5.anode, Onderdeel1.D4
  N40: LED6.cathode, R2.Pin_1
  N41: LED6.anode, Onderdeel1.D5_PWM
  N42: LED7.cathode, R1.Pin_1
  N43: LED7.anode, Onderdeel1.D6_PWM
  N44: LED8.cathode, R3.Pin_1
  N45: LED8.anode, Onderdeel1.D7
  N46: S1.Pin_1, S1.Pin_2, R17.Pin_1, Onderdeel1.A1
  N47: S2.Pin_1, S2.Pin_2, R16.Pin_1, Onderdeel1.A0
  N48: S3.Pin_1, S3.Pin_2, R15.Pin_1, Onderdeel1.D9_PWM
  N49: S4.Pin_1, S4.Pin_2, R14.Pin_1, Onderdeel1.D10_PWM/SS
  N50: S5.Pin_1, S5.Pin_2, R10.Pin_1
  N51: S6.Pin_1, S6.Pin_2, R13.Pin_1
  N52: S7.Pin_1, S7.Pin_2, R11.Pin_1
  N53: S8.Pin_1, S8.Pin_2, R12.Pin_1
  N54: J1.pin1, R9.Pin_0
  N55: J1.pin2, Onderdeel1.D11_PWM/MOSI
